# Fritzing sketch FlameAlarm (saved by Fritzing 0.9.3b)

parts:
  Part1 = Arduino Nano (Rev3.0)
  A1 = MH-FMD buzzer
  LED1 = LED - 5mm [color="Red (633nm)" package="5 mm [THT]"]
  Mod1 = KY-026 Flame Sensor Module [package="Breakout board"]

nets:
  N1: Part1.GND, LED1.cathode, Mod1.G
  N2: Part1.D2, LED1.anode
  N3: Part1.5V, Mod1.+
  N4: Part1.A0, Mod1.A0
  N5: Part1.D13/SCK, A1.Pin_2

custom parts:
  MH-FMD buzzer: MH-FMD buzzer.
  KY-026 Flame Sensor Module: KY-026 Flame Sensor Module reacts in the presence of fire.
